// Logisim project pk16.circ as structural Verilog
module opcode_reader (
  input  [7:0] memory_read
);

  wire [7:0] undriven;

  Register register_1 (.D(undriven));  // open: en, clk, Q, clr
  Register register_2 (.D(undriven));  // open: en, clk, Q, clr
endmodule
